// Logisim project ALU.circ as structural Verilog: 1 circuit, main circuit ALU
module ALU (
  input  [31:0] A,
  input  [31:0] B,
  input  [4:0] Shift,
  input  [3:0] Codop,
  input  CarryIn,
  input  in_6,
  input  [31:0] in_7,
  output [31:0] S,
  output [3:0] Flags
);

  wire AddC, not_1_out, SubC, subtractor_1_bout;
  wire [31:0] A_AND_B, A_XOR_B, ADC, B_LSL, B_LSR, B_LSR_ARITH, B_LSR_ROT, BIC, CMN, CMP, MUL, MVN,
       not_3_out, ORR, RSB, SBC;

  Multiplexer #(.select(4), .width(32)) multiplexer_1 (
    .in0(A_AND_B), .in1(A_XOR_B), .in2(B_LSL), .in3(B_LSR), .in4(B_LSR_ARITH), .in5(ADC), .in6(SBC),
    .in7(B_LSR_ROT), .in8(in_7), .in9(RSB), .in10(CMP), .in11(CMN), .in12(ORR), .in13(MUL), .in14(BIC),
    .in15(MVN), .out(S), .sel(Codop));
  Multiplexer #(.select(4)) multiplexer_2 (
    .in0(in_6), .in1(in_6), .in2(in_6), .in3(in_6), .in4(in_6), .in5(AddC), .in6(SubC), .in7(in_6),
    .in8(in_6), .in9(in_6), .in10(SubC), .in11(AddC), .in12(in_6), .in13(in_6), .in14(in_6), .in15(in_6),
    .out(Flags[2]), .sel(Codop));
  assign A_XOR_B = A ^ B;  // XOR_Gate xor_1, 32 bits wide
  assign A_AND_B = A & B;  // AND_Gate and_1, 32 bits wide
  Shifter #(.width(32)) shifter_1 (.in(B), .\dist (Shift), .out(B_LSL));
  Shifter #(.shift("lr"), .width(32)) shifter_2 (.in(B), .\dist (Shift), .out(B_LSR));
  Shifter #(.shift("ar"), .width(32)) shifter_3 (.in(B), .\dist (Shift), .out(B_LSR_ARITH));
  Adder #(.width(32)) adder_1 (.a(A), .b(B), .out(ADC), .cin(CarryIn), .cout(AddC));
  not not_1 (not_1_out, CarryIn);
  Subtractor #(.width(32)) subtractor_1 (.a(B), .b(A), .out(SBC), .bin(not_1_out), .bout(subtractor_1_bout));
  not not_2 (SubC, subtractor_1_bout);
  Shifter #(.shift("rr"), .width(32)) shifter_4 (.in(B), .\dist (Shift), .out(B_LSR_ROT));
  // AND_Gate and_2 has open pins: in0=A, in1=B, out=open
  Subtractor #(.width(32)) subtractor_2 (.a(in_7), .b(A), .out(RSB));  // open: bin, bout
  Subtractor #(.width(32)) subtractor_3 (.a(B), .b(A), .out(CMP));  // open: bin, bout
  Adder #(.width(32)) adder_2 (.a(A), .b(B), .out(CMN));  // open: cin, cout
  assign not_3_out = ~A;  // NOT_Gate not_3, 32 bits wide
  assign MVN = ~A;  // NOT_Gate not_4, 32 bits wide
  assign ORR = A | B;  // OR_Gate or_1, 32 bits wide
  Multiplier #(.width(32)) multiplier_1 (.a(A), .b(B), .out(MUL));  // open: cin, cout
  assign BIC = B & not_3_out;  // AND_Gate and_3, 32 bits wide

  // Other names for the same wires on the sheet: Cero1Bit = in_6; cIn = CarryIn; N = Flags[0]; Z = Flags[1];
  //   C = Flags[2]; V = Flags[3]; Cero[31:0] = in_7; TST[31:0] = in_7

  // Notes on the sheet:
  //   Note: for ROR, C = N
  //   Note 2: assume that shift > 0 for LSL and LSR
endmodule
