// Logisim project Ctl_Conditional.circ as structural Verilog: 1 circuit, main circuit Conditional
module Conditional (
  input  Enable,
  input  [15:0] Instruction,
  input  Z,
  input  C,
  input  N,
  input  V,
  output [10:0] Offset,
  output Verified
);

  wire CANDZ, CORZ, GT, LE, NEQV, not_1_out, not_2_out, not_3_out, not_4_out, not_5_out, not_6_out,
       not_7_out, not_8_out, not_9_out, sortie, treize;
  wire [2:0] undriven_2;
  wire [7:0] undriven;
  wire [10:0] imm811bits;

  BitSelector bitselector_1 (.in(undriven), .out(treize), .sel(undriven_2));
  assign imm811bits = {{3{Instruction[7]}}, Instruction[7:0]};  // Bit_Extender bit_extender_1
  Multiplexer #(.width(11)) multiplexer_1 (.in0(imm811bits), .in1(Instruction[10:0]), .out(Offset), .sel(treize));
  Comparator #(.width(1)) comparator_1 (.a(N), .b(V), .eq(NEQV));  // open: gt, lt
  or or_1 (LE, Z, not_1_out);
  not not_1 (not_1_out, NEQV);
  not not_2 (not_2_out, C);
  and and_1 (Verified, sortie, Enable);
  or or_2 (CORZ, not_2_out, Z);
  and and_2 (CANDZ, C, not_3_out);
  not not_3 (not_3_out, Z);
  not not_4 (not_4_out, Z);
  and and_3 (GT, not_4_out, NEQV);
  not not_5 (not_5_out, Z);
  not not_6 (not_6_out, C);
  not not_7 (not_7_out, N);
  not not_8 (not_8_out, V);
  not not_9 (not_9_out, NEQV);
  Multiplexer #(.select(4)) multiplexer_2 (
    .in0(Z), .in1(not_5_out), .in2(C), .in3(not_6_out), .in4(N), .in5(not_7_out), .in6(V), .in7(not_8_out),
    .in8(CANDZ), .in9(CORZ), .in10(NEQV), .in11(not_9_out), .in12(GT), .in13(LE), .in14(1'b1), .in15(1'b0),
    .out(sortie), .sel(Instruction[11:8]));

  // Other names for the same wires on the sheet: imm8[7:0] = Instruction[7:0]; imm11[10:0] = Instruction[10:0];
  //   Instruct[15:0] = Instruction; cond[3:0] = Instruction[11:8]
endmodule
