// Logisim project Ctl_Load_Store.circ as structural Verilog: 1 circuit, main circuit Load_Store
module Load_Store (
  input  [15:0] Instruction,
  input  [31:0] Stack_Pointer,
  input  Enable,
  input  Clk,
  input  Reset,
  output [2:0] Rmd,
  output [31:0] RAM_Addr,
  output Load,
  output PC_Hold,
  output Store
);

  wire and_3_out, comparator_1_eq, comparator_1_lt, not_1_out;
  wire [31:0] bit_extender_1_out, shifter_1_out;

  Comparator #(.width(1)) comparator_1 (
    .a(1'b1), .b(Instruction[11]), .eq(comparator_1_eq), .lt(comparator_1_lt));  // open: gt
  assign bit_extender_1_out = {{24{Instruction[7]}}, Instruction[7:0]};  // Bit_Extender bit_extender_1
  Shifter #(.width(32)) shifter_1 (.in(bit_extender_1_out), .\dist (5'b00010), .out(shifter_1_out));
  and and_1 (Load, Enable, comparator_1_eq);
  and and_2 (Store, Enable, comparator_1_lt);
  Adder #(.width(32)) adder_1 (.a(shifter_1_out), .b(Stack_Pointer), .out(RAM_Addr));  // open: cin, cout
  and and_3 (and_3_out, not_1_out, Load);
  not not_1 (not_1_out, PC_Hold);
  D_Flip_Flop d_ff_1 (.D(and_3_out), .clk(Clk), .Q(PC_Hold), .reset(Reset));  // open: Qn, preset

  assign Rmd = Instruction[10:8];

  // Other names for the same wires on the sheet: rt[2:0] = Instruction[10:8]; SP[31:0] = Stack_Pointer

  // Notes on the sheet:
  //   Instruction: pull=down
  //   Delay load and hold PC for 1 cycle for the RAM to send out requested data 
endmodule
